# Fritzing sketch Untitled Sketch (saved by Fritzing 0.9.3b)
circuit board: 18.1846cm x 12.7742cm
breadboards: 1

parts:
  LCD1 = LCD screen
  R1 = Rotary Potentiometer (Small) [maximum_resistance=100kΩ package=THT]
  Part1 = Arduino Uno (Rev3)
  R2 = Resistor [tolerance=±5% resistance=220 package=THT]
  R3 = Resistor [tolerance=±5% resistance=220 package=THT]
  J1 = Piezo Speaker
  LED1 = LED - 5mm [color="Red (633nm)" package="5 mm [THT]"]

nets:
  VSS: LCD1.VSS, LCD1.R/W, LCD1.LED-, R1.leg1, Part1.GND, R3.Pin_1, J1.pin1, LED1.cathode
  VDD: LCD1.VDD, LCD1.LED+, R1.leg2, Part1.5V
  N1: LCD1.V0, R1.wiper
  N2: LCD1.RS, Part1.D8
  N3: LCD1.E, Part1.D9_PWM
  N4: LCD1.DB4, Part1.D4
  N5: LCD1.DB5, Part1.D5_PWM
  N6: LCD1.DB6, Part1.D6_PWM
  N7: LCD1.DB7, Part1.D7
  N8: Part1.A5/SCL, R2.Pin_1, R3.Pin_0
  N9: Part1.D11_PWM/MOSI, LED1.anode
  N10: R2.Pin_0, J1.pin2

// code stored in the sketch: sensor.ino
 

#include <LiquidCrystal.h>
LiquidCrystal lcd(8, 9, 4, 5, 6, 7);

int analogInput=A5;
float vout;
float vin;
float R1 = 980.0;
float R2 = 980.0;
int value;

void setup() {
  
  pinMode(analogInput, INPUT);
  lcd.begin(16, 2);
  
  lcd.setCursor(2, 0);
  lcd.print("Initializing");
  lcd.setCursor(4, 1);
  lcd.print("EE Wave");
  
  delay(1500);
  lcd.clear();
pinMode(11, OUTPUT);
}
void loop() {
  lcd.setCursor(2, 0);
  lcd.print("DC Voltmeter");

  value = analogRead(analogInput);
  vout = (value * 5)/1.023;
  vin = vout / (R2 / (R1 + R2));
  
  if (vin < 0.09)
  {
    vin = 0.0;
    digitalWrite (11,LOW);
  
  }
  
  else if (vin>0.09)
  {digitalWrite (11,HIGH); }
  lcd.setCursor(0, 1);
  lcd.print("Input mv :");
  lcd.print(vin);
  delay(300);
  lcd.clear();

  
}
